// Logisim project Układ wejściowy.circ as structural Verilog: 1 circuit, main circuit main
module main (
  input  in_1,
  input  in_2
);

  wire and_1_out, and_2_out, and_3_out, and_4_out, n7474_1_p5, n7474_1_p6, n7474_1_p13, or_1_out, or_2_out;

  and and_1 (and_1_out, n7474_1_p6, in_1);
  and and_2 (and_2_out, in_1, n7474_1_p13);
  and and_3 (and_3_out, in_1, n7474_1_p5);
  or or_1 (or_1_out, and_1_out, and_2_out);
  or or_2 (or_2_out, and_2_out, and_3_out);
  and and_4 (and_4_out, n7474_1_p5, n7474_1_p13);
  LED led_1 (.in(and_4_out));
  // _7474 7474_1: pin names not known; wires that end beside it: 1'b0, or_1_out, in_2, 1'b0, n7474_1_p5, n7474_1_p6, 1'b0, 1'b1, 1'b0, or_2_out, in_2, 1'b0, n7474_1_p13
endmodule
