// Logisim project Układ z JK (wersja początkowa).circ as structural Verilog: 1 circuit, main circuit main
module main (
  input  in_1
);

  wire and_1_out, and_2_out, clock_1_out, n7476_1_p10, n7476_1_p13, n7476_1_p14, not_1_out, or_1_out;

  Clock clock_1 (.out(clock_1_out));
  not not_1 (not_1_out, in_1);
  or or_1 (or_1_out, n7476_1_p14, not_1_out);
  and and_1 (and_1_out, n7476_1_p10, in_1);
  // _7476 7476_1: pin names not known; wires that end beside it: clock_1_out, 1'b0, 1'b0, in_1, 1'b1, clock_1_out, 1'b0, 1'b0, or_1_out, n7476_1_p10, 1'b0, not_1_out, n7476_1_p13, n7476_1_p14, and_1_out
  and and_2 (and_2_out, n7476_1_p10, n7476_1_p13);
  LED led_1 (.in(and_2_out));
endmodule
