// Logisim project uklad-nand-Ł.circ as structural Verilog: 1 circuit, main circuit main
module main (
  input  X,
  input  CLK
);

  wire n7474_1_p1, n7474_1_p6, n7474_1_p7, nand_1_out, nand_2_out, nand_3_out, nor_1_out, X_nY1_out, XY1_out,
       XY2_out;

  nand X_nY1 (X_nY1_out, n7474_1_p6, X);
  nand XY2 (XY2_out, X, n7474_1_p1);
  nand XY1 (XY1_out, X, n7474_1_p7);
  nand nand_1 (nand_1_out, X_nY1_out, XY2_out);
  nand nand_2 (nand_2_out, XY2_out, XY1_out);
  // _7474 7474_1: pin names not known; wires that end beside it: n7474_1_p1, CLK, nand_2_out, 1'b1, 1'b0, n7474_1_p6, n7474_1_p7, CLK, nand_1_out
  LED Y1 (.in(n7474_1_p7));
  LED Y2 (.in(n7474_1_p1));
  nand nand_3 (nand_3_out, n7474_1_p7, n7474_1_p1);
  LED Y1Y2 (.in(nor_1_out));
  nor nor_1 (nor_1_out, nand_3_out, nand_3_out);
endmodule
